# Fritzing sketch Self balancing circuit (saved by Fritzing 0.9.3b)
breadboards: 1

parts:
  Part2 = Arduino Uno (Rev3)  # not connected
  U1 = LIPO-2000mAh [package=lipo-2000]
  GY1 = MPU-6050 Board GY-521 [form="♀ (female)" package=THT]
  U2 = ESP32-38PinWide [part_number=ESP32-38PinWide]
  U4 = POT [package=pot_mammoth]
  Arduino_CNC_Shield_V3_00_1 = Arduino_CNC_V3.00
  U5 = POT [package=pot_mammoth]
  U6 = POT [package=pot_mammoth]
  IC1 = Voltage Regulator [package=78xxl]
  J1 = Basic Servo
  J2 = Basic Servo

nets:
  N1: U1.+, U2.VIN, Arduino_CNC_Shield_V3_00_1.POWER_-, IC1.IN
  GND: U1.-, GY1.pin2, U2.GPIO11, U4.S, Arduino_CNC_Shield_V3_00_1.POWER_+, U5.S, U6.S, IC1.GND, J1.gnd, J2.gnd
  VCC: GY1.pin1, U4.E, U5.E, U6.E, IC1.OUT, J1.vcc, J2.vcc
  N2: GY1.pin3, Arduino_CNC_Shield_V3_00_1.SCL_/_Probe
  N3: GY1.pin4, Arduino_CNC_Shield_V3_00_1.SDA
  N4: U2.GPIO3, Arduino_CNC_Shield_V3_00_1.TX
  N5: U2.GPIO1, Arduino_CNC_Shield_V3_00_1.RX
  N6: U4.A, Arduino_CNC_Shield_V3_00_1.Resume
  N7: Arduino_CNC_Shield_V3_00_1.End_Stops_Z+_(and_Z-)_/_SpnEn, J1.pulse
  N8: Arduino_CNC_Shield_V3_00_1.End_Stops_Y+_(and_Y-), J2.pulse
  N9: Arduino_CNC_Shield_V3_00_1.SpnEn_/_Z_Limit, Arduino_CNC_Shield_V3_00_1.E-STOP
  N10: Arduino_CNC_Shield_V3_00_1.Abort, U5.A
  N11: Arduino_CNC_Shield_V3_00_1.Hold, U6.A

custom parts:
  MPU-6050 Board GY-521: Acelerometro y Giroscopio MPU-6050 Board GY-521
  ESP32-38PinWide: Generic 38-Pin ESP32 with wide format (only access to one side of pins on a breadboard) based on Stephen Lilley's HiLetgo ESP-WROOM-32 ESP32 ESP-32S Development Board.
  Arduino_CNC_V3.00: Protoneer Arduino CNC Shield V3.00 If using Grbl V0.9: The “A” axis can not be used (yet). The “SCL” (Arduino A5) pin is now used for 'Probing' input. The “End Stops Z+ & Z-” (Arduino D11) and “SpnEn” (Arduino D12) have been switched!
